// Logisim project sapMultiplicador.circ as structural Verilog: 19 circuits, main circuit main
module main (
  input  Reset,
  output [3:0] \Endereço ,
  output [3:0] Dados,
  output [15:0] out_4,
  output out_5,
  output out_6,
  output out_7,
  output out_8,
  output out_9,
  output out_10,
  output out_11,
  output out_12
);

  wire CLK, Clock_out, controlador_sequencializador_1_hlt, Cp, Ea, EnM, Ep, Eu, nCE, nEi, nLa, nLb, nLi, nLm,
       nLo, not_1_out, not_2_out, not_3_out, not_4_out, \registrador_instruções_1_i4 ,
       \registrador_instruções_1_i5 , \registrador_instruções_1_i6 , \registrador_instruções_1_i7 , Su;
  wire [3:0] rem_1_remout;
  wire [7:0] acumulador_1_a_out_ula, registrador_b_1_b_dataout;

  Clock Clock (.out(Clock_out));
  not not_1 (not_1_out, CLK);
  not not_2 (not_2_out, Reset);
  not not_3 (not_3_out, nCE);
  assign CLK = not_4_out ? Clock_out : 1'bz;  // Controlled_Buffer controlled_buffer_1
  not not_4 (not_4_out, controlador_sequencializador_1_hlt);
  REM rem_1 (.in_1(Dados), .nLm(nLm), .CLK(CLK), .REMOut(rem_1_remout));
  Contador_Programa contador_programa_1 (.Cp(Cp), .nCLK(not_1_out), .nCLR(not_2_out), .Ep(Ep), .Cp_Out(Dados));
  \Memória_RAM  \memória_ram_1  (.in_1(rem_1_remout), .nCE(not_3_out), .CLK(CLK), .out_4({\Endereço , Dados}));
  \Registrador_Instruções  \registrador_instruções_1  (
    .in_1({\Endereço , Dados}), .nLi(nLi), .CLK(CLK), .CLR(Reset), .nEi(nEi), .out_6({\Endereço , Dados}),
    .I4(\registrador_instruções_1_i4 ), .I5(\registrador_instruções_1_i5 ),
    .I6(\registrador_instruções_1_i6 ), .I7(\registrador_instruções_1_i7 ));
  Controlador_Sequencializador controlador_sequencializador_1 (
    .CLR(Reset), .I7(\registrador_instruções_1_i7 ), .Ep(Ep), .Cp(Cp), .I6(\registrador_instruções_1_i6 ),
    .I5(\registrador_instruções_1_i5 ), .I4(\registrador_instruções_1_i4 ),
    .HLT(controlador_sequencializador_1_hlt), .Ea(Ea), .Su(Su), .Eu(Eu), .nLo(nLo), .nLl(nLi), .CLK(CLK),
    .nLm(nLm), .nEl(nEi), .nCE(nCE), .nLb(nLb), .nLa(nLa), .EnM(EnM));
  Acumulador acumulador_1 (
    .A_In({\Endereço , Dados}), .nLa(nLa), .CLK(CLK), .Ea(Ea), .A_Out_ULA(acumulador_1_a_out_ula),
    .A_Out({\Endereço , Dados}));
  Somador_Subtrator somador_subtrator_1 (
    .Su(Su), .B_data(registrador_b_1_b_dataout), .A_dataOut2({\Endereço , Dados}),
    .A_data(acumulador_1_a_out_ula), .Eu(Eu));
  Registrador_B registrador_b_1 (
    .B_dataIn({\Endereço , Dados}), .B_dataOut(registrador_b_1_b_dataout), .nLb(nLb), .CLK(CLK));
  Hex_Digit_Display hex_digit_display_1 (.value({out_5, out_6, out_7, out_8}));  // open: dp
  \Indicação_Visual  \indicação_visual_1  (
    .Input({\Endereço , Dados}), .Output({out_5, out_6, out_7, out_8, out_9, out_10, out_11, out_12}),
    .nLo(nLo), .CLK(CLK), .CLR(Reset));
  Multiplicador multiplicador_1 (.A(acumulador_1_a_out_ula), .B(registrador_b_1_b_dataout), .\Saída (out_4));
  DotMatrix #(.matrixcols(8), .matrixrows(1), .dotshape("circle")) dotmatrix_1 (
    .col0(out_5), .col1(out_6), .col2(out_7), .col3(out_8), .col4(out_9), .col5(out_10), .col6(out_11),
    .col7(out_12));
  Hex_Digit_Display hex_digit_display_2 (.value({out_9, out_10, out_11, out_12}));  // open: dp

  // Other names for the same wires on the sheet: CLR = Reset

  // Notes on the sheet:
  //   SAP-1 COM COMPARADOR
  //   Arquitetura de Computadores I
  //   Aluno:
  //   - Túlio Furst Akar
  //   Instruções:
  //   - 0000: pegar o valor
  //   - 0001: somar o valor
  //   - 0010: subtrair o valor
  //   - 0011: multiplica o valor
  //   - 1110: exibir o valor
  //   - 1111: interromper o circuito
  //   Circuito original:
  //   - André Santos Alves
  //   - Nathan de Araújo Cunha Lisboa
  //   - Pedro Malta Boscatti
  //   - Sophia Damasceno Satuf
endmodule

module Contador_Programa (
  input  Cp,
  input  nCLK,
  input  nCLR,
  input  Ep,
  output [3:0] Cp_Out
);

  wire not_1_out;
  wire [3:0] counter_1_q;

  not not_1 (not_1_out, nCLR);
  Counter #(.width(4), .max('hf), .trigger("falling")) counter_1 (
    .count(Cp), .Q(counter_1_q), .clk(nCLK), .clr(not_1_out));  // open: load, D, carry
  assign Cp_Out = Ep ? counter_1_q : 4'bz;  // Controlled_Buffer controlled_buffer_1
endmodule

module REM (
  input  [3:0] in_1,
  input  nLm,
  input  CLK,
  output [3:0] REMOut
);

  wire not_1_out;

  not not_1 (not_1_out, nLm);
  Register #(.width(4)) register_1 (.D(in_1), .en(not_1_out), .Q(REMOut), .clk(CLK));  // open: clr
endmodule

module \Memória_RAM  (
  input  [3:0] in_1,
  input  nCE,
  input  CLK,
  output [7:0] out_4
);

  RAM #(.addrWidth(4)) ram_1 (.addr(in_1), .data(out_4), .sel(nCE), .clk(CLK), .ld(nCE));  // open: clr
endmodule

module \Registrador_Instruções  (
  input  [7:0] in_1,
  input  nLi,
  input  CLK,
  input  CLR,
  input  nEi,
  output [7:0] out_6,
  output I4,
  output I5,
  output I6,
  output I7
);

  wire not_1_out, not_2_out;
  wire [3:0] register_1_q;
  wire [7:0] bit_extender_1_out;

  not not_1 (not_1_out, nLi);
  not not_2 (not_2_out, nEi);
  Register register_1 (.D(in_1), .en(not_1_out), .Q({I7, I6, I5, I4, register_1_q}), .clk(CLK), .clr(CLR));
  assign bit_extender_1_out = {{4{1'b0}}, register_1_q};  // Bit_Extender bit_extender_1
  assign out_6 = not_2_out ? bit_extender_1_out : 8'bz;  // Controlled_Buffer controlled_buffer_1
endmodule

module Acumulador (
  input  [7:0] A_In,
  input  nLa,
  input  CLK,
  input  Ea,
  output [7:0] A_Out_ULA,
  output [7:0] A_Out
);

  wire not_1_out;

  not not_1 (not_1_out, nLa);
  Register register_1 (.D(A_In), .en(not_1_out), .Q(A_Out_ULA), .clk(CLK));  // open: clr
  assign A_Out = Ea ? A_Out_ULA : 8'bz;  // Controlled_Buffer controlled_buffer_1
endmodule

module Somador_Subtrator (
  input  Su,
  input  [7:0] B_data,
  input  [7:0] A_data,
  input  Eu,
  output [7:0] A_dataOut2
);

  wire [7:0] adder_1_out, xor_1_out;

  assign xor_1_out = {8{Su}} ^ B_data;  // XOR_Gate xor_1, 8 bits wide
  Adder adder_1 (.a(xor_1_out), .b(A_data), .out(adder_1_out), .cin(Su));  // open: cout
  assign A_dataOut2 = Eu ? adder_1_out : 8'bz;  // Controlled_Buffer controlled_buffer_1
endmodule

module Registrador_B (
  input  [7:0] B_dataIn,
  input  nLb,
  input  CLK,
  output [7:0] B_dataOut
);

  wire not_1_out;

  Register register_1 (.D(B_dataIn), .en(not_1_out), .Q(B_dataOut), .clk(CLK));  // open: clr
  not not_1 (not_1_out, nLb);
endmodule

module Controlador_Sequencializador (
  input  CLK,
  input  CLR,
  input  I7,
  input  I6,
  input  I5,
  input  I4,
  output Ep,
  output Cp,
  output Ea,
  output Su,
  output Eu,
  output nLo,
  output nLl,
  output HLT,
  output nLm,
  output nCE,
  output nEl,
  output nLa,
  output EnM,
  output nLb
);

  wire c39_1_out_7, c39_1_out_8, c39_1_out_9, c39_1_out_10, c40_1_out_7, c40_1_out_8, c40_1_out_9,
       c40_1_out_10, c41_1_out_8, c41_1_out_9, c41_1_out_10, c41_1_out_11, c41_2_out_10, c41_2_out_11,
       c43_1_out_6, c43_1_out_7, c43_1_out_8, c44_1_out_9, c44_1_out_10, c45_1_out_7, c45_1_out_8,
       c46_1_out_6, decodificador_1_add, decodificador_1_cmp, decodificador_1_lda, decodificador_1_out,
       decodificador_1_sub, nor_1_out, not_1_out, not_2_out, not_3_out, not_4_out, not_5_out, not_7_out,
       shift_register_1_q2, shift_register_1_q3, shift_register_1_q4, shift_register_1_q5, T4_out, T5_out,
       T6_out;

  Decodificador decodificador_1 (
    .LDA(decodificador_1_lda), .ADD(decodificador_1_add), .SUB(decodificador_1_sub),
    .OUT(decodificador_1_out), .HLT(HLT), .l7(I7), .l6(I6), .l5(I5), .l4(I4), .CMP(decodificador_1_cmp));
  C39 c39_1 (
    ._1(decodificador_1_lda), ._4(decodificador_1_add), ._9(decodificador_1_sub), ._10(shift_register_1_q3),
    ._12(decodificador_1_lda), ._13(shift_register_1_q4), .out_7(c39_1_out_7), .out_8(c39_1_out_8),
    .out_9(c39_1_out_9), .out_10(c39_1_out_10));
  not not_1 (not_1_out, CLK);
  C40 c40_1 (
    ._1(decodificador_1_add), ._4(decodificador_1_sub), ._5(shift_register_1_q4), ._9(decodificador_1_lda),
    ._12(decodificador_1_add), ._13(shift_register_1_q3), .out_7(c40_1_out_7), .out_8(c40_1_out_8),
    .out_9(c40_1_out_9), .out_10(c40_1_out_10));
  C44 c44_1 (
    .in_1(Ep), .in_2(c39_1_out_7), .in_3(c39_1_out_8), .in_4(c39_1_out_9), .in_5(shift_register_1_q2),
    .in_6(c39_1_out_10), .in_7(c40_1_out_7), .in_8(c40_1_out_8), .out_9(c44_1_out_9), .out_10(c44_1_out_10));
  not not_2 (not_2_out, c44_1_out_10);
  not not_3 (not_3_out, c44_1_out_9);
  and and_1 (nCE, not_2_out, T5_out);
  and and_2 (nLm, not_3_out, T4_out);
  Shift_Register #(.length(6)) shift_register_1 (
    .in(nor_1_out), .clk(not_1_out), .clr(CLR), .q0(Ep), .q1(Cp), .q2(shift_register_1_q2),
    .q3(shift_register_1_q3), .q4(shift_register_1_q4), .q5(shift_register_1_q5));  // open: shift, out, load, d0, d1, d2, d3, d4, d5
  C41 c41_1 (
    ._1(decodificador_1_sub), ._2(shift_register_1_q3), ._4(decodificador_1_lda), ._5(shift_register_1_q4),
    ._9(decodificador_1_add), ._12(decodificador_1_sub), ._13(shift_register_1_q5), .out_8(c41_1_out_8),
    .out_9(c41_1_out_9), .out_10(c41_1_out_10), .out_11(c41_1_out_11));
  C45 c45_1 (
    .in_1(c40_1_out_9), .in_2(c40_1_out_10), .in_3(c41_1_out_8), .in_4(c41_1_out_9), .in_5(c41_1_out_10),
    .in_6(c41_1_out_11), .out_7(c45_1_out_7), .out_8(c45_1_out_8));
  and and_3 (nEl, not_5_out, T4_out);
  C41 c41_2 (
    ._1(decodificador_1_out), ._2(shift_register_1_q3), ._4(decodificador_1_sub), ._5(shift_register_1_q5),
    ._9(decodificador_1_add), ._12(decodificador_1_sub), ._13(shift_register_1_q5), .out_8(Ea), .out_9(Su),
    .out_10(c41_2_out_10), .out_11(c41_2_out_11));
  not not_4 (not_4_out, c45_1_out_8);
  not not_5 (not_5_out, c45_1_out_7);
  and and_4 (nLa, not_4_out, T6_out);
  C46 c46_1 (
    .in_1(c41_2_out_10), .in_2(c41_2_out_11), .in_3(c43_1_out_6), .in_4(c43_1_out_7), .out_5(Eu),
    .out_6(c46_1_out_6));
  not not_6 (EnM, T6_out);
  C43 c43_1 (
    ._1(decodificador_1_add), ._4(decodificador_1_sub), ._5(shift_register_1_q4), ._9(decodificador_1_out),
    ._10(shift_register_1_q3), .out_6(c43_1_out_6), .out_7(c43_1_out_7), .out_8(c43_1_out_8));
  not not_7 (not_7_out, c46_1_out_6);
  and and_5 (nLb, not_7_out, T5_out);
  nor nor_1 (nor_1_out, Ep, Cp, shift_register_1_q2, shift_register_1_q3, shift_register_1_q4);
  not not_8 (nLo, c43_1_out_8);
  not not_9 (nLl, shift_register_1_q2);
  nand T4 (T4_out, decodificador_1_cmp, shift_register_1_q3);
  nand T5 (T5_out, shift_register_1_q4, decodificador_1_cmp);
  nand T6 (T6_out, shift_register_1_q5, decodificador_1_cmp);
endmodule

module Decodificador (
  input  l7,
  input  l6,
  input  l5,
  input  l4,
  output LDA,
  output ADD,
  output SUB,
  output OUT,
  output HLT,
  output CMP
);

  wire and_1_out, and_2_out, and_3_out, and_4_out, and_5_out, and_6_out, not_1_out, not_2_out, not_3_out,
       not_4_out;

  not not_1 (not_1_out, l7);
  not not_2 (not_2_out, l6);
  not not_3 (not_3_out, l5);
  not not_4 (not_4_out, l4);
  and and_1 (and_1_out, not_1_out, not_2_out, not_3_out, not_4_out);
  buf buffer_1 (LDA, and_1_out);
  buf buffer_2 (ADD, and_2_out);
  and and_2 (and_2_out, not_1_out, not_2_out, not_3_out, l4);
  buf buffer_3 (SUB, and_3_out);
  and and_3 (and_3_out, not_1_out, not_2_out, l5, not_4_out);
  and and_4 (and_4_out, l7, l6, l5, not_4_out);
  buf buffer_4 (OUT, and_4_out);
  and and_5 (and_5_out, l7, l6, l5, l4);
  buf buffer_5 (HLT, and_5_out);
  buf buffer_6 (CMP, and_6_out);
  and and_6 (and_6_out, l5, l4, not_2_out, not_1_out);
endmodule

module C39 (
  input  _1,
  input  _4,
  input  _9,
  input  _10,
  input  _13,
  input  _12,
  output out_7,
  output out_8,
  output out_9,
  output out_10
);

  and and_1 (out_7, _1, _10);
  and and_2 (out_8, _4, _10);
  and and_3 (out_9, _9, _10);
  and and_4 (out_10, _12, _13);
endmodule

module C40 (
  input  _1,
  input  _4,
  input  _5,
  input  _9,
  input  _12,
  input  _13,
  output out_7,
  output out_8,
  output out_9,
  output out_10
);

  and and_1 (out_7, _1, _5);
  and and_2 (out_8, _4, _5);
  and and_3 (out_9, _9, _13);
  and and_4 (out_10, _12, _13);
endmodule

module C41 (
  input  _4,
  input  _5,
  input  _12,
  input  _13,
  input  _1,
  input  _2,
  input  _9,
  output out_8,
  output out_9,
  output out_10,
  output out_11
);

  and and_1 (out_8, _1, _2);
  and and_2 (out_9, _4, _5);
  and and_3 (out_10, _9, _13);
  and and_4 (out_11, _12, _13);
endmodule

module C43 (
  input  _1,
  input  _4,
  input  _5,
  input  _9,
  input  _10,
  output out_6,
  output out_7,
  output out_8
);

  and and_1 (out_6, _1, _5);
  and and_2 (out_7, _4, _5);
  and and_3 (out_8, _9, _10);
endmodule

module C44 (
  input  in_1,
  input  in_2,
  input  in_3,
  input  in_4,
  input  in_5,
  input  in_6,
  input  in_7,
  input  in_8,
  output out_9,
  output out_10
);

  or or_1 (out_9, in_1, in_2, in_3, in_4);
  or or_2 (out_10, in_5, in_6, in_7, in_8);
endmodule

module C45 (
  input  in_1,
  input  in_2,
  input  in_3,
  input  in_4,
  input  in_5,
  input  in_6,
  output out_7,
  output out_8
);

  or or_1 (out_7, in_1, in_2, in_3);
  or or_2 (out_8, in_4, in_5, in_6);
endmodule

module C46 (
  input  in_1,
  input  in_2,
  input  in_3,
  input  in_4,
  output out_5,
  output out_6
);

  or or_1 (out_5, in_1, in_2);
  or or_2 (out_6, in_3, in_4);
endmodule

module \Indicação_Visual  (
  input  [7:0] Input,
  input  nLo,
  input  CLK,
  input  CLR,
  output [7:0] Output
);

  wire not_1_out;

  not not_1 (not_1_out, nLo);
  Register register_1 (.D(Input), .en(not_1_out), .Q(Output), .clk(CLK), .clr(CLR));
endmodule

module Multiplicador (
  input  [7:0] A,
  input  [7:0] B,
  output [15:0] \Saída 
);

  wire [8:0] adder_1_out, adder_2_out, adder_4_out, adder_6_out, and_1_out, and_2_out, and_3_out, and_4_out,
       and_5_out, and_6_out, and_7_out, and_8_out;
  wire [8:1] adder_3_out, adder_5_out;
  wire [8:8] adder_3_cout, adder_5_cout;

  assign and_1_out = {1'b0, B} & {9{A[0]}};  // AND_Gate and_1, 9 bits wide
  assign and_2_out = {B, 1'b0} & {9{A[1]}};  // AND_Gate and_2, 9 bits wide
  assign and_3_out = {9{A[2]}} & {B, 1'b0};  // AND_Gate and_3, 9 bits wide
  assign and_4_out = {9{A[3]}} & {B, 1'b0};  // AND_Gate and_4, 9 bits wide
  assign and_5_out = {9{A[4]}} & {B, 1'b0};  // AND_Gate and_5, 9 bits wide
  assign and_6_out = {9{A[5]}} & {B, 1'b0};  // AND_Gate and_6, 9 bits wide
  assign and_7_out = {9{A[6]}} & {B, 1'b0};  // AND_Gate and_7, 9 bits wide
  assign and_8_out = {9{A[7]}} & {B, 1'b0};  // AND_Gate and_8, 9 bits wide
  Adder #(.width(9)) adder_1 (
    .a(and_1_out), .b(and_2_out), .out({adder_1_out[7:0], \Saída [0]}), .cout(adder_1_out[8]));  // open: cin
  Adder #(.width(9)) adder_2 (
    .a(adder_1_out), .b(and_3_out), .out({adder_2_out[7:0], \Saída [1]}), .cout(adder_2_out[8]));  // open: cin
  Adder #(.width(9)) adder_3 (
    .a(adder_2_out), .b(and_4_out), .out({adder_3_out, \Saída [2]}), .cout(adder_3_cout[8]));  // open: cin
  Adder #(.width(9)) adder_4 (
    .a({adder_3_cout[8], adder_3_out}), .b(and_5_out), .out({adder_4_out[7:0], \Saída [3]}),
    .cout(adder_4_out[8]));  // open: cin
  Adder #(.width(9)) adder_5 (
    .a(adder_4_out), .b(and_6_out), .out({adder_5_out, \Saída [4]}), .cout(adder_5_cout[8]));  // open: cin
  Adder #(.width(9)) adder_6 (
    .a({adder_5_cout[8], adder_5_out}), .b(and_7_out), .out({adder_6_out[7:0], \Saída [5]}),
    .cout(adder_6_out[8]));  // open: cin
  Adder #(.width(9)) adder_7 (.a(adder_6_out), .b(and_8_out), .out(\Saída [14:6]), .cout(\Saída [15]));  // open: cin
endmodule
